// Digital circuit 7_seg_driver.dig as structural Verilog
module _7_seg_driver (
  input  in_1,
  input  in_2,
  input  in_3,
  input  in_4
);

  wire _7432_1_pin1, _7432_1_pin2, _7432_1_pin3, _7432_1_pin5, _7432_1_pin6, _7432_1_pin8, _7432_1_pin10,
       _7432_1_pin11, _7432_1_pin13, _7432_2_pin1, _7432_2_pin2, _7432_2_pin3, _7432_2_pin5, _7432_2_pin6,
       _7432_2_pin8, _7432_2_pin10, _7432_2_pin13, _7432_3_pin3, _7432_3_pin6, _7432_3_pin8, _7432_3_pin11,
       _7432_4_pin3, _7432_4_pin6, _7432_4_pin8, _7432_4_pin11, _7432_5_pin3, _7432_5_pin6, _7432_5_pin8,
       _7432_5_pin11, _7432_6_pin3, _7432_6_pin6, _7432_6_pin8, _7432_6_pin11, _7432_7_pin3, _7432_7_pin6,
       _7432_7_pin8, _7432_7_pin11, _7432_8_pin3, _7432_8_pin6, _7432_8_pin8, _7432_8_pin11, _7432_9_pin3,
       _7432_9_pin6, _7432_9_pin8, _7432_9_pin11, _7432_10_pin3, _7432_10_pin6, _7432_10_pin8,
       _7432_10_pin11, _7432_11_pin3, _7432_11_pin6, _7432_11_pin8, _7432_11_pin11, _7432_12_pin3,
       _7432_12_pin6, _7432_12_pin8, _7432_12_pin11, _7442_1_pin1, _7442_1_pin2, _7442_1_pin3, _7442_1_pin4,
       _7442_1_pin5, _7442_1_pin6, _7442_1_pin7, _7442_1_pin9, _7442_1_pin10, _7442_1_pin11, SEG_E_pin2,
       SEG_E_pin3, SEG_E_pin6, SEG_E_pin8, SEG_E_pin11;

  _7432 _7432_1 (
    .pin1(_7432_1_pin1), .pin2(_7432_1_pin2), .pin3(_7432_1_pin3), .pin4(_7432_1_pin3), .pin5(_7432_1_pin5),
    .pin6(_7432_1_pin6), .pin7(1'b0), .pin8(_7432_1_pin8), .pin9(_7432_1_pin6), .pin10(_7432_1_pin10),
    .pin11(_7432_1_pin11), .pin12(_7432_1_pin8), .pin13(_7432_1_pin13), .pin14(1'b1));
  _7432 _7432_2 (
    .pin1(_7432_2_pin1), .pin2(_7432_2_pin2), .pin3(_7432_2_pin3), .pin4(_7432_2_pin3), .pin5(_7432_2_pin5),
    .pin6(_7432_2_pin6), .pin7(1'b0), .pin8(_7432_2_pin8), .pin9(_7432_2_pin6), .pin10(_7432_2_pin10),
    .pin11(_7432_1_pin1), .pin12(_7432_2_pin8), .pin13(_7432_2_pin13), .pin14(1'b1));
  _7432 SEG_E (
    .pin1(_7432_2_pin1), .pin2(SEG_E_pin2), .pin3(SEG_E_pin3), .pin4(SEG_E_pin3), .pin5(_7432_1_pin2),
    .pin6(SEG_E_pin6), .pin7(1'b0), .pin8(SEG_E_pin8), .pin9(SEG_E_pin6), .pin10(_7432_1_pin10),
    .pin11(SEG_E_pin11), .pin12(SEG_E_pin8), .pin13(1'b0), .pin14(1'b1));
  _7432 _7432_3 (
    .pin1(_7432_2_pin1), .pin2(_7432_2_pin10), .pin3(_7432_3_pin3), .pin4(_7432_3_pin3),
    .pin5(_7432_2_pin13), .pin6(_7432_3_pin6), .pin7(1'b0), .pin8(_7432_3_pin8), .pin9(_7432_3_pin6),
    .pin10(_7432_1_pin2), .pin11(_7432_3_pin11), .pin12(_7432_3_pin8), .pin13(_7432_1_pin10), .pin14(1'b1));
  _7432 _7432_4 (
    .pin1(_7432_3_pin11), .pin2(_7432_1_pin13), .pin3(_7432_4_pin3), .pin4(_7432_4_pin3), .pin5(1'b0),
    .pin6(_7432_4_pin6), .pin7(1'b0), .pin8(_7432_4_pin8), .pin9(_7432_4_pin6), .pin10(1'b0),
    .pin11(_7432_4_pin11), .pin12(_7432_4_pin8), .pin13(1'b0), .pin14(1'b1));
  not not_1 (_7432_1_pin5, _7442_1_pin9);
  not not_2 (_7432_2_pin13, _7442_1_pin6);
  not not_3 (_7432_1_pin2, _7442_1_pin7);
  not not_4 (_7432_1_pin10, _7442_1_pin10);
  not not_5 (_7432_1_pin13, _7442_1_pin11);
  not not_6 (_7432_2_pin5, _7442_1_pin4);
  not not_7 (_7432_2_pin10, _7442_1_pin5);
  not not_8 (_7432_2_pin2, _7442_1_pin2);
  not not_9 (SEG_E_pin2, _7442_1_pin3);
  _7432 _7432_5 (
    .pin1(_7432_2_pin1), .pin2(SEG_E_pin2), .pin3(_7432_5_pin3), .pin4(_7432_5_pin3), .pin5(_7432_2_pin5),
    .pin6(_7432_5_pin6), .pin7(1'b0), .pin8(_7432_5_pin8), .pin9(_7432_5_pin6), .pin10(_7432_2_pin13),
    .pin11(_7432_5_pin11), .pin12(_7432_5_pin8), .pin13(_7432_1_pin2), .pin14(1'b1));
  _7442 _7442_1 (
    .pin1(_7442_1_pin1), .pin2(_7442_1_pin2), .pin3(_7442_1_pin3), .pin4(_7442_1_pin4), .pin5(_7442_1_pin5),
    .pin6(_7442_1_pin6), .pin7(_7442_1_pin7), .pin8(1'b0), .pin9(_7442_1_pin9), .pin10(_7442_1_pin10),
    .pin11(_7442_1_pin11), .pin12(in_1), .pin13(in_2), .pin14(in_3), .pin15(in_4), .pin16(1'b1));
  not not_10 (_7432_2_pin1, _7442_1_pin1);
  _7432 _7432_6 (
    .pin1(_7432_5_pin11), .pin2(_7432_1_pin5), .pin3(_7432_6_pin3), .pin4(_7432_6_pin3),
    .pin5(_7432_1_pin10), .pin6(_7432_6_pin6), .pin7(1'b0), .pin8(_7432_6_pin8), .pin9(_7432_6_pin6),
    .pin10(_7432_1_pin13), .pin11(_7432_6_pin11), .pin12(_7432_6_pin8), .pin13(1'b0), .pin14(1'b1));
  _7432 _7432_7 (
    .pin1(_7432_2_pin1), .pin2(SEG_E_pin2), .pin3(_7432_7_pin3), .pin4(_7432_7_pin3), .pin5(_7432_2_pin5),
    .pin6(_7432_7_pin6), .pin7(1'b0), .pin8(_7432_7_pin8), .pin9(_7432_7_pin6), .pin10(_7432_2_pin13),
    .pin11(_7432_7_pin11), .pin12(_7432_7_pin8), .pin13(_7432_1_pin2), .pin14(1'b1));
  Seven_Seg seven_seg_1 (
    .a(_7432_6_pin11), .b(_7432_10_pin11), .c(_7432_1_pin11), .d(_7432_8_pin11), .e(SEG_E_pin11),
    .f(_7432_4_pin11), .g(_7432_12_pin11), .dp(1'b0));
  _7432 _7432_8 (
    .pin1(_7432_7_pin11), .pin2(_7432_1_pin10), .pin3(_7432_8_pin3), .pin4(_7432_8_pin3),
    .pin5(_7432_1_pin13), .pin6(_7432_8_pin6), .pin7(1'b0), .pin8(_7432_8_pin8), .pin9(_7432_8_pin6),
    .pin10(1'b0), .pin11(_7432_8_pin11), .pin12(_7432_8_pin8), .pin13(1'b0), .pin14(1'b1));
  _7432 _7432_9 (
    .pin1(_7432_2_pin1), .pin2(_7432_2_pin2), .pin3(_7432_9_pin3), .pin4(_7432_9_pin3), .pin5(SEG_E_pin2),
    .pin6(_7432_9_pin6), .pin7(1'b0), .pin8(_7432_9_pin8), .pin9(_7432_9_pin6), .pin10(_7432_2_pin5),
    .pin11(_7432_9_pin11), .pin12(_7432_9_pin8), .pin13(_7432_2_pin10), .pin14(1'b1));
  _7432 _7432_10 (
    .pin1(_7432_9_pin11), .pin2(_7432_1_pin5), .pin3(_7432_10_pin3), .pin4(_7432_10_pin3),
    .pin5(_7432_1_pin10), .pin6(_7432_10_pin6), .pin7(1'b0), .pin8(_7432_10_pin8), .pin9(_7432_10_pin6),
    .pin10(_7432_1_pin13), .pin11(_7432_10_pin11), .pin12(_7432_10_pin8), .pin13(1'b0), .pin14(1'b1));
  _7432 _7432_11 (
    .pin1(SEG_E_pin2), .pin2(_7432_2_pin5), .pin3(_7432_11_pin3), .pin4(_7432_11_pin3), .pin5(_7432_2_pin10),
    .pin6(_7432_11_pin6), .pin7(1'b0), .pin8(_7432_11_pin8), .pin9(_7432_11_pin6), .pin10(_7432_2_pin13),
    .pin11(_7432_11_pin11), .pin12(_7432_11_pin8), .pin13(_7432_1_pin2), .pin14(1'b1));
  _7432 _7432_12 (
    .pin1(_7432_11_pin11), .pin2(_7432_1_pin10), .pin3(_7432_12_pin3), .pin4(_7432_12_pin3),
    .pin5(_7432_1_pin13), .pin6(_7432_12_pin6), .pin7(1'b0), .pin8(_7432_12_pin8), .pin9(_7432_12_pin6),
    .pin10(1'b0), .pin11(_7432_12_pin11), .pin12(_7432_12_pin8), .pin13(1'b0), .pin14(1'b1));

  // Notes on the sheet:
  //   SEG C
  //   SEG F
  //   SEG D
  //   SEG A
  //   SEG B
  //   SEG G
endmodule
