// Digital circuit calculator_final_project.dig as structural Verilog
module calculator_final_project (
  input  clk,
  input  clk_2,
  input  clk_3,
  output [7:0] out_1,
  output [7:0] out_3,
  output [15:0] out_6
);

  wire _0_out, _1_out, _2_out, _3_out, _4_out, _5_out, _6_out, _7_out, _8_out, _9_out, and_1_out, and_2_out,
       button_1_out, button_2_out, button_3_out, button_4_out, CL_out, counter_1_out, eq_out, not_1_out,
       not_2_out, not_4_out, not_6_out, not_7_out, not_8_out, or_1_out, or_2_out, or_3_out, or_6_out,
       or_7_out, or_8_out, or_9_out, or_10_out, or_11_out, or_12_out, or_13_out, or_14_out, or_15_out,
       or_17_out, plus_2_q, plus_out, rs_ff_as_2_q, rs_ff_as_3_q, rs_ff_as_q;
  wire [0:0] not_3_out, not_5_out;
  wire [3:0] priorityencoder_1_num;
  wire [3:3] counter_2_out, counter_3_out;
  wire [7:0] add_1_s, add_2_s, add_3_s, and_3_out, and_4_out, and_5_out, and_6_out, and_9_out, and_10_out,
       and_11_out, and_13_out, and_14_out, and_16_out, and_17_out, and_19_out, and_20_out, and_22_out,
       div_1_q, or_4_out, or_5_out, rom_1_d, rom_1_d_2, rom_2_d, rom_2_d_2, sub_1_s;
  wire [7:7] and_7_out, and_8_out, and_12_out, and_15_out, and_18_out, and_21_out;
  wire [15:0] mul_1_mul, mul_2_mul, mul_3_mul, or_16_out;

  Counter counter_1 (.en(1'b1), .C(button_1_out), .clr(1'b0), .out(counter_1_out));  // open: ovf
  Button button_1 (.out(button_1_out));
  not not_1 (not_1_out, counter_1_out);
  or or_1 (or_1_out, _5_out, _6_out, _7_out, _8_out, _9_out);
  or or_2 (or_2_out, or_3_out, or_1_out);
  and and_1 (and_1_out, or_2_out, not_1_out);
  Counter counter_2 (.en(1'b1), .C(and_1_out), .clr(1'b0), .out(counter_2_out[3]));  // open: ovf
  Seven_Seg seven_seg_1 (
    .a(rom_2_d_2[0]), .b(rom_2_d_2[1]), .c(rom_2_d_2[2]), .d(rom_2_d_2[3]), .e(rom_2_d_2[4]),
    .f(rom_2_d_2[5]), .g(rom_2_d_2[6]), .dp(rom_2_d_2[7]));
  or or_3 (or_3_out, _0_out, _1_out, _2_out, _3_out, _4_out);
  and and_2 (and_2_out, or_2_out, counter_1_out);
  Counter counter_3 (.en(1'b1), .C(and_2_out), .clr(1'b0), .out(counter_3_out[3]));  // open: ovf
  LED led_1 (.in(not_2_out));
  not not_2 (not_2_out, counter_1_out);
  not not_3 (not_3_out[0], counter_2_out[3]);
  not not_4 (not_4_out, counter_2_out[3]);
  Seven_Seg seven_seg_2 (
    .a(rom_2_d[0]), .b(rom_2_d[1]), .c(rom_2_d[2]), .d(rom_2_d[3]), .e(rom_2_d[4]), .f(rom_2_d[5]),
    .g(rom_2_d[6]), .dp(rom_2_d[7]));
  PriorityEncoder #(.Selector_Bits(4)) priorityencoder_1 (
    .in0(_0_out), .in1(_1_out), .in2(_2_out), .in3(_3_out), .in4(_4_out), .in5(_5_out), .in6(_6_out),
    .in7(_7_out), .in8(_8_out), .in9(_9_out), .in10(1'b0), .in11(1'b0), .in12(1'b0), .in13(1'b0),
    .in14(1'b0), .in15(1'b0), .num(priorityencoder_1_num));  // open: any
  not not_5 (not_5_out[0], counter_3_out[3]);
  not not_6 (not_6_out, counter_3_out[3]);
  assign and_3_out = 8'h1 & {{7{1'b0}}, not_3_out[0]};  // And and_3, 8 bits wide
  assign and_4_out = 8'ha & {4'b0000, counter_2_out[3], 1'b0, counter_2_out[3], 1'b0};  // And and_4, 8 bits wide
  assign and_5_out = 8'h1 & {{7{1'b0}}, not_5_out[0]};  // And and_5, 8 bits wide
  assign and_6_out = 8'ha & {4'b0000, counter_3_out[3], 1'b0, counter_3_out[3], 1'b0};  // And and_6, 8 bits wide
  assign or_4_out = and_3_out | and_4_out;  // Or or_4, 8 bits wide
  LED led_2 (.in(plus_2_q));
  LED led_3 (.in(rs_ff_as_q));
  LED led_4 (.in(rs_ff_as_2_q));
  LED led_5 (.in(rs_ff_as_3_q));
  Button _7 (.out(_7_out));
  Button _4 (.out(_4_out));
  Button _1 (.out(_1_out));
  Button eq (.out(eq_out));
  assign or_5_out = and_5_out | and_6_out;  // Or or_5, 8 bits wide
  Button _8 (.out(_8_out));
  Button _5 (.out(_5_out));
  Button _2 (.out(_2_out));
  Button _0 (.out(_0_out));
  Mul #(.Bits(8)) mul_1 (.a({4'b0000, priorityencoder_1_num}), .b(or_4_out), .mul(mul_1_mul));
  Button _9 (.out(_9_out));
  Button _6 (.out(_6_out));
  Button _3 (.out(_3_out));
  Button CL (.out(CL_out));
  Mul #(.Bits(8)) mul_2 (.a({4'b0000, priorityencoder_1_num}), .b(or_5_out), .mul(mul_2_mul));
  Seven_Seg seven_seg_3 (
    .a(rom_1_d_2[0]), .b(rom_1_d_2[1]), .c(rom_1_d_2[2]), .d(rom_1_d_2[3]), .e(rom_1_d_2[4]),
    .f(rom_1_d_2[5]), .g(rom_1_d_2[6]), .dp(rom_1_d_2[7]));
  Button plus (.out(plus_out));
  Button button_2 (.out(button_2_out));
  Button button_3 (.out(button_3_out));
  Button button_4 (.out(button_4_out));
  or or_6 (or_6_out, and_1_out, CL_out);
  or or_7 (or_7_out, and_2_out, CL_out);
  not not_7 (not_7_out, CL_out);
  LED led_6 (.in(counter_1_out));
  Seven_Seg seven_seg_4 (
    .a(rom_1_d[0]), .b(rom_1_d[1]), .c(rom_1_d[2]), .d(rom_1_d[3]), .e(rom_1_d[4]), .f(rom_1_d[5]),
    .g(rom_1_d[6]), .dp(rom_1_d[7]));
  and and_7 (and_7_out[7], not_8_out, not_6_out);
  not not_8 (not_8_out, CL_out);
  Add #(.Bits(8)) add_1 (.a(mul_1_mul[7:0]), .b(and_9_out), .c_i(1'b0), .s(add_1_s));  // open: c_o
  and and_8 (and_8_out[7], not_7_out, not_4_out);
  or or_8 (or_8_out, or_13_out, CL_out);
  or or_9 (or_9_out, or_12_out, CL_out);
  or or_10 (or_10_out, or_14_out, CL_out);
  or or_11 (or_11_out, or_15_out, CL_out);
  RS_FF_AS plus_2 (.S(plus_out), .R(or_9_out), .Q(plus_2_q));  // open: nQ
  RS_FF_AS rs_ff_as (.S(button_2_out), .R(or_8_out), .Q(rs_ff_as_q));  // open: nQ
  RS_FF_AS rs_ff_as_2 (.S(button_3_out), .R(or_10_out), .Q(rs_ff_as_2_q));  // open: nQ
  RS_FF_AS rs_ff_as_3 (.S(button_4_out), .R(or_11_out), .Q(rs_ff_as_3_q));  // open: nQ
  Add #(.Bits(8)) add_2 (.a(mul_2_mul[7:0]), .b(and_10_out), .c_i(1'b0), .s(add_2_s));  // open: c_o
  Register #(.Bits(8)) register_1 (.D(add_1_s), .C(clk_2), .en(or_6_out), .Q(out_3));
  assign and_9_out = {8{and_8_out[7]}} & out_3;  // And and_9, 8 bits wide
  or or_12 (or_12_out, button_2_out, button_3_out, button_4_out);
  or or_13 (or_13_out, button_4_out, button_3_out, plus_out);
  or or_14 (or_14_out, button_4_out, button_2_out, plus_out);
  or or_15 (or_15_out, button_3_out, button_2_out, plus_out);
  Register #(.Bits(8)) register_2 (.D(add_2_s), .C(clk), .en(or_7_out), .Q(out_1));
  assign and_10_out = {8{and_7_out[7]}} & out_1;  // And and_10, 8 bits wide
  Add #(.Bits(8)) add_3 (.a(and_11_out), .b(and_13_out), .c_i(1'b0), .s(add_3_s));  // open: c_o
  assign and_11_out = out_3 & {8{and_12_out[7]}};  // And and_11, 8 bits wide
  and and_12 (and_12_out[7], plus_2_q, eq_out);
  assign and_13_out = {8{and_12_out[7]}} & out_1;  // And and_13, 8 bits wide
  Seven_Seg_Hex seven_seg_hex_1 (.d(out_6[15:12]), .dp(1'b0));
  assign and_14_out = out_3 & {8{and_15_out[7]}};  // And and_14, 8 bits wide
  Seven_Seg_Hex seven_seg_hex_2 (.d(out_6[11:8]), .dp(1'b0));
  assign or_16_out = {{8{1'b0}}, add_3_s} | {{8{1'b0}}, sub_1_s} | mul_3_mul | {{8{1'b0}}, div_1_q};  // Or or_16, 16 bits wide
  Sub #(.Bits(8)) sub_1 (.a(and_14_out), .b(and_16_out), .c_i(1'b0), .s(sub_1_s));  // open: c_o
  and and_15 (and_15_out[7], rs_ff_as_q, eq_out);
  ROM #(.bigEndian("true"), .AddrBits(8), .Bits(16)) rom_1 (.A(out_1), .sel(1'b1), .D({rom_1_d_2, rom_1_d}));
  ROM #(.bigEndian("true"), .AddrBits(8), .Bits(16)) rom_2 (.A(out_3), .sel(1'b1), .D({rom_2_d_2, rom_2_d}));
  Seven_Seg_Hex seven_seg_hex_3 (.d(out_6[7:4]), .dp(1'b0));
  Register #(.Bits(16)) register_3 (.D(or_16_out), .C(clk_3), .en(or_17_out), .Q(out_6));
  assign and_16_out = {8{and_15_out[7]}} & out_1;  // And and_16, 8 bits wide
  Seven_Seg_Hex seven_seg_hex_4 (.d(out_6[3:0]), .dp(1'b0));
  assign and_17_out = out_3 & {8{and_18_out[7]}};  // And and_17, 8 bits wide
  or or_17 (or_17_out, CL_out, eq_out);
  Mul #(.Bits(8)) mul_3 (.a(and_17_out), .b(and_19_out), .mul(mul_3_mul));
  and and_18 (and_18_out[7], rs_ff_as_2_q, eq_out);
  assign and_19_out = {8{and_18_out[7]}} & out_1;  // And and_19, 8 bits wide
  assign and_20_out = out_3 & {8{and_21_out[7]}};  // And and_20, 8 bits wide
  Div #(.Bits(8)) div_1 (.a(and_20_out), .b(and_22_out), .q(div_1_q));  // open: r
  and and_21 (and_21_out[7], rs_ff_as_3_q, eq_out);
  assign and_22_out = {8{and_21_out[7]}} & out_1;  // And and_22, 8 bits wide

  // Notes on the sheet:
  //   clk: Hz: 10
  //   clk_2: Hz: 10
  //   clk_3: Hz: 10
  //   CISLO
  //   DVOJCIFRA 0
  //   Multiply by 1 (nothing)
  //   Multiply by 10
  //   +
  //   _
  //   *
  //   /
  //   DVOJCIFRA 1
  //   =
  //   contents of rom_1 (hex, n*v repeats v):
  //   3f3f,3f06,3f5b,3f4f,3f66,3f6d,3f7c,3f07,3f7f,3f6f,63f,606,65b
  //   ,64f,666,66d,67c,607,67f,66f,5b3f,5b06,5b5b,5b4f,5b66,5b6d,5b7c,5b7c
  //   ,5b7f,5b6f,4f3f,4f06,4f5b,4f4f,4f66,4f6d,4f7c,4f07,4f7f,4f6f,663f
  //   ,6606,665b,664f,6666,666d,667c,6607,667f,666f,6d3f,6d06,6d5b,6d4f
  //   ,6d66,6d6d,6d7c,6d07,6d7f,6d6f,7c3f,7c06,7c5b,7c4f,7c66,7c6d,7c7c
  //   ,7c07,7c7f,7c6f,73f,706,75b,74f,766,76d,77c,707,77f,76f,7f3f,7f06
  //   ,7f5b,7f4f,7f66,7f6d,7f7c,7f07,7f7f,7f6f,6f3f,6f06,6f5b,6f4f,6f66
  //   ,6f6d,6f7c,6f07,6f7f,6f6f
  //   contents of rom_2 (hex, n*v repeats v):
  //   3f3f,3f06,3f5b,3f4f,3f66,3f6d,3f7c,3f07,3f7f,3f6f,63f,606,65b
  //   ,64f,666,66d,67c,607,67f,66f,5b3f,5b06,5b5b,5b4f,5b66,5b6d,5b7c,5b7c
  //   ,5b7f,5b6f,4f3f,4f06,4f5b,4f4f,4f66,4f6d,4f7c,4f07,4f7f,4f6f,663f
  //   ,6606,665b,664f,6666,666d,667c,6607,667f,666f,6d3f,6d06,6d5b,6d4f
  //   ,6d66,6d6d,6d7c,6d07,6d7f,6d6f,7c3f,7c06,7c5b,7c4f,7c66,7c6d,7c7c
  //   ,7c07,7c7f,7c6f,73f,706,75b,74f,766,76d,77c,707,77f,76f,7f3f,7f06
  //   ,7f5b,7f4f,7f66,7f6d,7f7c,7f07,7f7f,7f6f,6f3f,6f06,6f5b,6f4f,6f66
  //   ,6f6d,6f7c,6f07,6f7f,6f6f
endmodule
