// Digital circuit memory.dig as structural Verilog
module memory (
  input  WRITE,
  input  _3,
  input  _4,
  input  [3:0] SET,
  input  CLEAR_ALL,
  output [3:0] out_1,
  output [3:0] out_7,
  output [3:0] out_8,
  output [3:0] out_9
);

  wire and_1_out, and_2_out, and_3_out, and_4_out, and_5_out, and_6_out, and_7_out, and_8_out, not_1_out,
       not_2_out, not_3_out, not_4_out;

  D_FF_AS #(.Bits(4)) d_ff_as_1 (.Set(1'b0), .D(SET), .C(and_1_out), .Clr(CLEAR_ALL), .Q(out_1));  // open: nQ
  and and_1 (and_1_out, WRITE, and_2_out);
  and and_2 (and_2_out, not_2_out, not_1_out);
  not not_1 (not_1_out, _4);
  not not_2 (not_2_out, _3);
  D_FF_AS #(.Bits(4)) d_ff_as_2 (.Set(1'b0), .D(SET), .C(and_3_out), .Clr(CLEAR_ALL), .Q(out_7));  // open: nQ
  and and_3 (and_3_out, WRITE, and_4_out);
  D_FF_AS #(.Bits(4)) d_ff_as_3 (.Set(1'b0), .D(SET), .C(and_5_out), .Clr(CLEAR_ALL), .Q(out_8));  // open: nQ
  and and_4 (and_4_out, _3, not_3_out);
  not not_3 (not_3_out, _4);
  and and_5 (and_5_out, WRITE, and_6_out);
  and and_6 (and_6_out, not_4_out, _4);
  not not_4 (not_4_out, _3);
  D_FF_AS #(.Bits(4)) d_ff_as_4 (.Set(1'b0), .D(SET), .C(and_7_out), .Clr(CLEAR_ALL), .Q(out_9));  // open: nQ
  and and_7 (and_7_out, WRITE, and_8_out);
  and and_8 (and_8_out, _3, _4);

  // Notes on the sheet:
  //   Address choice
  //   M0
  //   M1
  //   M2
  //   M3
endmodule
